# Fritzing sketch attiny weight lcd (saved by Fritzing 0.9.3b)

parts:
  Bauteil1 = LCD1602-I2C
  U1 = ATTINY45 [package=so]
  U2 = LM2596 step down module
  Bauteil2 = HX711 Weighing Sensor Module
  Load_Cell1 = Load Cell - Red/white/black/green

nets:
  GND: Bauteil1.GND, U1.GND, U2.IN-, U2.OUT-, Bauteil2.GND
  VCC: Bauteil1.VCC, U1.PB5(NRES), U1.VCC, U2.OUT+, Bauteil2.VCC
  N1: Bauteil1.SDA, U1.PB0(MOSI)
  N2: Bauteil1.SCL, U1.PB2(SCK_ADC1)
  N3: U1.PB4(ADC2), Bauteil2.DO/RX
  N4: U1.PB1(MISO), Bauteil2.CK/TX
  N5: Bauteil2.E+, Load_Cell1.wire1
  N6: Bauteil2.E-, Load_Cell1.wire3
  N7: Bauteil2.A+, Load_Cell1.wire2
  N8: Bauteil2.A-, Load_Cell1.wire4

notes:
  24V input
  5V

custom parts:
  LCD1602-I2C: A standard character display, usually with 2x16 characters. Comes in many colors with LCM1602 IIC attached.
  LM2596 step down module: LM2596 DC-DC step down power supply module 3 A.
  Load Cell - Red/white/black/green: A rectangle load cell/weighting pressure Sensor with four wires - Red, white, black, green. Normally corresponding with E+, E-, A+, A- respectively.
